# Fritzing sketch wiring_diagram (saved by Fritzing 1.0.4)
perfboards: 1

parts:
  Bauteil1 = Arduino Nano 33 BLE Sense
  PWM1 = PCA9685 16x12-bit PWM Breakout
  PWM2 = PCA9685 16x12-bit PWM Breakout
  J2 = Screw terminal - 2 pins [package=THT]
  J1 = Basic Servo
  S2 = Limit Switch [package="Breakout Board"]
  S3 = Limit Switch [package="Breakout Board"]
  S4 = Limit Switch [package="Breakout Board"]
  S5 = Limit Switch [package="Breakout Board"]
  S6 = Limit Switch [package="Breakout Board"]
  S7 = Limit Switch [package="Breakout Board"]
  J3 = Basic Servo
  J4 = Basic Servo
  J5 = Basic Servo
  J6 = Basic Servo
  J7 = Basic Servo
  J8 = Basic Servo
  J9 = Basic Servo
  J10 = Basic Servo
  J11 = Basic Servo
  J12 = Basic Servo
  J13 = Basic Servo
  J14 = Basic Servo
  J15 = Basic Servo
  J16 = Basic Servo
  J17 = Basic Servo
  J18 = Basic Servo
  J19 = Basic Servo

nets:
  N1: Bauteil1.GND, Bauteil1.A7, PWM1.no_name_yet#501, PWM1.no_name_yet#601, PWM1.no_name_yet#1004, PWM1.no_name_yet#1005, PWM1.no_name_yet#1006, PWM1.no_name_yet#1008, PWM1.no_name_yet#1009, PWM1.no_name_yet#1010, PWM1.no_name_yet#1012, PWM1.no_name_yet#1013, PWM1.no_name_yet#1014, PWM2.no_name_yet#501, PWM2.no_name_yet#1005, PWM2.no_name_yet#1006, PWM2.no_name_yet#1007, PWM2.no_name_yet#1008, PWM2.no_name_yet#1010, PWM2.no_name_yet#1011, PWM2.no_name_yet#1013, PWM2.no_name_yet#1014, PWM2.no_name_yet#1015, J2.pin2, S2.G, S3.G, S4.G, S5.G, S6.G, S7.G
  N2: Bauteil1.D8, S4.S
  N3: Bauteil1.D9~, S3.S
  N4: Bauteil1.D10~, S2.S
  N5: Bauteil1.D11/MOSI, S5.S
  N6: Bauteil1.D12~/MISO, S6.S
  N7: Bauteil1.VIN, PWM1.no_name_yet#104, PWM1.no_name_yet#105, PWM1.no_name_yet#106, PWM1.no_name_yet#108, PWM1.no_name_yet#109, PWM1.no_name_yet#110, PWM1.no_name_yet#112, PWM1.no_name_yet#113, PWM1.no_name_yet#114, PWM1.no_name_yet#506, PWM1.no_name_yet#606, PWM2.no_name_yet#105, PWM2.no_name_yet#106, PWM2.no_name_yet#107, PWM2.no_name_yet#108, PWM2.no_name_yet#110, PWM2.no_name_yet#111, PWM2.no_name_yet#113, PWM2.no_name_yet#114, PWM2.no_name_yet#115, PWM2.no_name_yet#506, J2.pin1
  N8: Bauteil1.A5, PWM1.no_name_yet#503, PWM1.no_name_yet#603, PWM2.no_name_yet#503
  N9: Bauteil1.A4, PWM1.no_name_yet#504, PWM1.no_name_yet#604, PWM2.no_name_yet#504
  N10: Bauteil1.A0, S7.S
  N11: Bauteil1.3V3, PWM1.no_name_yet#505, PWM1.no_name_yet#605, PWM2.no_name_yet#505, S5.V, S6.V, S7.V
  N12: PWM1.no_name_yet#4, J1.pulse
  N13: PWM1.no_name_yet#5, J3.pulse
  N14: PWM1.no_name_yet#6, J4.pulse
  N15: PWM1.no_name_yet#8, J5.pulse
  N16: PWM1.no_name_yet#9, J6.pulse
  N17: PWM1.no_name_yet#10, J7.pulse
  N18: PWM1.no_name_yet#12, J10.pulse
  N19: PWM1.no_name_yet#13, J9.pulse
  N20: PWM1.no_name_yet#14, J8.pulse
  N21: PWM2.no_name_yet#5, J17.pulse
  N22: PWM2.no_name_yet#6, J18.pulse
  N23: PWM2.no_name_yet#7, J19.pulse
  N24: PWM2.no_name_yet#8, J14.pulse
  N25: PWM2.no_name_yet#10, J15.pulse
  N26: PWM2.no_name_yet#11, J16.pulse
  N27: PWM2.no_name_yet#13, J13.pulse
  N28: PWM2.no_name_yet#14, J12.pulse
  N29: PWM2.no_name_yet#15, J11.pulse

notes:
  6V Lipo Battery

custom parts:
  Arduino Nano 33 BLE Sense: The Nano 33 BLE Sense (without headers) is Arduino’s 3.3V AI enabled board in the smallest available form factor: 45x18mm! The Arduino Nano 33 BLE Sense is a completely new board on a well-known form factor. It comes with a series of embedded sensors: 9 axis inertial sensor: what makes this board ideal for wearable devices humidity, and temperature sensor: to get highly accurate measurements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
  Limit Switch: Generic limit switch commonly found on 3D printers. Typical lever microswitch mounted on a PCB board with a 3 pin JST XH connector.
